// Logisim project Microprocessor.circ as structural Verilog: 3 circuits, main circuit RegisterFile
module RegisterFile (
  input  WE,
  input  [3:0] WA,
  input  [7:0] INP,
  input  CLK,
  input  [3:0] RA1,
  input  [3:0] RA2,
  output [7:0] OUT2,
  output [7:0] OUT1
);

  wire decoder_1_out0, decoder_1_out1, decoder_1_out2, decoder_1_out3, decoder_1_out4, decoder_1_out5,
       decoder_1_out6, decoder_1_out7, decoder_1_out8, decoder_1_out9, decoder_1_out10, decoder_1_out11,
       decoder_1_out12, decoder_1_out13, decoder_1_out14, decoder_1_out15;
  wire [7:0] register_1_q, register_2_q, register_3_q, register_4_q, register_5_q, register_6_q,
       register_7_q, register_8_q, register_9_q, register_10_q, register_11_q, register_12_q, register_13_q,
       register_14_q, register_15_q, register_16_q;

  Register #(.Select("low")) register_1 (.D(INP), .en(decoder_1_out3), .Q(register_1_q), .clk(CLK));  // open: clr
  Register #(.Select("low")) register_2 (.D(INP), .en(decoder_1_out2), .Q(register_2_q), .clk(CLK));  // open: clr
  Register #(.Select("low")) register_3 (.D(INP), .en(decoder_1_out1), .Q(register_3_q), .clk(CLK));  // open: clr
  Register #(.Select("low")) register_4 (.D(INP), .en(decoder_1_out0), .Q(register_4_q), .clk(CLK));  // open: clr
  Decoder #(.select(4)) decoder_1 (
    .out0(decoder_1_out0), .out1(decoder_1_out1), .out2(decoder_1_out2), .out3(decoder_1_out3),
    .out4(decoder_1_out4), .out5(decoder_1_out5), .out6(decoder_1_out6), .out7(decoder_1_out7),
    .out8(decoder_1_out8), .out9(decoder_1_out9), .out10(decoder_1_out10), .out11(decoder_1_out11),
    .out12(decoder_1_out12), .out13(decoder_1_out13), .out14(decoder_1_out14), .out15(decoder_1_out15),
    .sel(WA), .en(WE));
  Register #(.Select("low")) register_5 (.D(INP), .en(decoder_1_out7), .Q(register_5_q), .clk(CLK));  // open: clr
  Register #(.Select("low")) register_6 (.D(INP), .en(decoder_1_out6), .Q(register_6_q), .clk(CLK));  // open: clr
  Register #(.Select("low")) register_7 (.D(INP), .en(decoder_1_out5), .Q(register_7_q), .clk(CLK));  // open: clr
  Register #(.Select("low")) register_8 (.D(INP), .en(decoder_1_out4), .Q(register_8_q), .clk(CLK));  // open: clr
  Register #(.Select("low")) register_9 (.D(INP), .en(decoder_1_out11), .Q(register_9_q), .clk(CLK));  // open: clr
  Register #(.Select("low")) register_10 (.D(INP), .en(decoder_1_out10), .Q(register_10_q), .clk(CLK));  // open: clr
  Register #(.Select("low")) register_11 (.D(INP), .en(decoder_1_out9), .Q(register_11_q), .clk(CLK));  // open: clr
  Register #(.Select("low")) register_12 (.D(INP), .en(decoder_1_out8), .Q(register_12_q), .clk(CLK));  // open: clr
  Register #(.Select("low")) register_13 (.D(INP), .en(decoder_1_out15), .Q(register_13_q), .clk(CLK));  // open: clr
  Register #(.Select("low")) register_14 (.D(INP), .en(decoder_1_out14), .Q(register_14_q), .clk(CLK));  // open: clr
  Register #(.Select("low")) register_15 (.D(INP), .en(decoder_1_out13), .Q(register_15_q), .clk(CLK));  // open: clr
  Register #(.Select("low")) register_16 (.D(INP), .en(decoder_1_out12), .Q(register_16_q), .clk(CLK));  // open: clr
  Multiplexer #(.select(4), .width(8), .enable("false")) multiplexer_1 (
    .in0(register_4_q), .in1(register_3_q), .in2(register_2_q), .in3(register_1_q), .in4(register_8_q),
    .in5(register_7_q), .in6(register_6_q), .in7(register_5_q), .in8(register_12_q), .in9(register_11_q),
    .in10(register_10_q), .in11(register_9_q), .in12(register_16_q), .in13(register_15_q),
    .in14(register_14_q), .in15(register_13_q), .out(OUT1), .sel(RA1));
  Multiplexer #(.select(4), .width(8), .enable("false")) multiplexer_2 (
    .in0(register_4_q), .in1(register_3_q), .in2(register_2_q), .in3(register_1_q), .in4(register_8_q),
    .in5(register_7_q), .in6(register_6_q), .in7(register_5_q), .in8(register_12_q), .in9(register_11_q),
    .in10(register_10_q), .in11(register_9_q), .in12(register_16_q), .in13(register_15_q),
    .in14(register_14_q), .in15(register_13_q), .out(OUT2), .sel(RA2));
endmodule

module ALU (
  input  [7:0] in_1,
  input  [7:0] in_2,
  input  [2:0] in_3,
  output [7:0] out_4,
  output out_5,
  output out_6,
  output out_7
);

  wire [7:0] adder_1_out, and_1_out, multiplier_1_out, negator_1_out, not_1_out, or_1_out, subtractor_1_out;

  assign not_1_out = ~in_1;  // NOT_Gate not_1, 8 bits wide
  assign and_1_out = in_1 & in_2;  // AND_Gate and_1, 8 bits wide
  assign or_1_out = in_1 | in_2;  // OR_Gate or_1, 8 bits wide
  Adder adder_1 (.a(in_1), .b(in_2), .out(adder_1_out));  // open: cin, cout
  Subtractor subtractor_1 (.a(in_1), .b(in_2), .out(subtractor_1_out));  // open: bin, bout
  Negator negator_1 (.in(in_1), .out(negator_1_out));
  Multiplier multiplier_1 (.a(in_1), .b(in_2), .out(multiplier_1_out));  // open: cin, cout
  Comparator comparator_1 (.a(in_1), .b(in_2), .gt(out_5), .eq(out_6), .lt(out_7));
  Multiplexer #(.select(3), .width(8), .enable("false")) multiplexer_1 (
    .in0(not_1_out), .in1(and_1_out), .in2(or_1_out), .in3(adder_1_out), .in4(subtractor_1_out),
    .in5(negator_1_out), .in6(multiplier_1_out), .out(out_4), .sel(in_3));  // open: in7
endmodule

module Program_Counter (
  input  in_1,
  input  in_2,
  input  in_3,
  output [7:0] out_4
);

  wire [7:0] adder_1_out;

  Adder adder_1 (.a(out_4), .b(8'h1), .out(adder_1_out));  // open: cin, cout
  Register #(.Select("low")) register_1 (.D(adder_1_out), .en(in_1), .Q(out_4), .clk(in_3), .clr(in_2));
endmodule
